# Fritzing sketch StanBaseBBPico (saved by Fritzing 0.9.6b)

parts:
  A4988_Board = Pololu A4988 [package=SO16]
  A4988_Board_2 = Pololu A4988 [package=SO16]
  R1 = Resistor [tolerance=±5% resistance=62k power=0.25 package=THT]
  R2 = Resistor [tolerance=±5% resistance=100k power=0.25 package=THT]
  C3 = Electrolytic Capacitor [capacitance=100µF voltage=50V package="200 mil [THT, electrolytic]"]
  C4 = Electrolytic Capacitor [capacitance=100µF voltage=50V package="200 mil [THT, electrolytic]"]
  Right_Motor = Header 4 [package=jst-4-pth]
  Left_Motor = Header 4 [package=jst-4-pth]
  Power_SW/BAT_(LiPo3S) = Header 2 [package=jst-2-pth]
  Tilt_Servo = Header 3 [package=molex-1x3_lock]
  Pan_Servo = Header 3 [package=molex-1x3_lock]
  Led_Matrix = Header 3 [package=molex-1x3_lock]
  Power_SW/BAT2_(5VUSB) = Header 2 [package=jst-2-pth]
  Picoboard = Raspberry Pi Pico
  BNO055 = 9-DOF Absolute Orientation IMU Fusion Breakout - BNO055
  Picoprobe = Raspberry Pi Pico

nets:
  N1: A4988_Board.MS1, A4988_Board_2.MS1, Picoboard.pin_19
  N2: A4988_Board.MS2, A4988_Board_2.MS2, Picoboard.pin_20
  VDD: A4988_Board.RESET, A4988_Board.VDD, A4988_Board_2.RESET, A4988_Board_2.VDD, Tilt_Servo.2, Pan_Servo.2, Led_Matrix.2, Power_SW/BAT2_(5VUSB).1
  N3: A4988_Board.SLEEP, A4988_Board_2.SLEEP, Picoboard.pin_16
  N4: A4988_Board.STEP, Picoboard.pin_11
  N5: A4988_Board.DIR, Picoboard.pin_12
  N6: A4988_Board.GND#8, A4988_Board_2.GND#8, Tilt_Servo.3, Pan_Servo.3, Led_Matrix.3, Power_SW/BAT2_(5VUSB).2, Picoboard.pin_33, Picoboard.pin_38, Picoboard.pin_42, BNO055.GND, Picoprobe.pin_38
  N7: A4988_Board.1B, Left_Motor.2
  N8: A4988_Board.1A, Left_Motor.1
  N9: A4988_Board.2A, Left_Motor.4
  N10: A4988_Board.2B, Left_Motor.3
  N11: A4988_Board.GND#14, A4988_Board_2.GND#14, R1.Pin_1, C3.-, C4.-, Power_SW/BAT_(LiPo3S).2
  N12: A4988_Board.VMOT, A4988_Board_2.VMOT, R2.Pin_0, C3.+, C4.+, Power_SW/BAT_(LiPo3S).1
  N13: A4988_Board_2.STEP, Picoboard.pin_14
  N14: A4988_Board_2.DIR, Picoboard.pin_15
  N15: A4988_Board_2.1B, Right_Motor.2
  N16: A4988_Board_2.1A, Right_Motor.1
  N17: A4988_Board_2.2A, Right_Motor.4
  N18: A4988_Board_2.2B, Right_Motor.3
  N19: R1.Pin_0, R2.Pin_1, Picoboard.pin_31, Picoprobe.pin_10
  N20: Tilt_Servo.1, Picoboard.pin_9
  N21: Pan_Servo.1, Picoboard.pin_10
  N22: Led_Matrix.1, Picoboard.pin_4
  N23: Picoboard.pin_1, Picoprobe.pin_7
  N24: Picoboard.pin_2, Picoprobe.pin_6
  N25: Picoboard.pin_6, BNO055.SDA_5V
  N26: Picoboard.pin_7, BNO055.SCL_5V, BNO055.RST_5V
  N27: Picoboard.pin_39, BNO055.5.0V, Picoprobe.pin_39
  N28: Picoboard.pin_41, Picoprobe.pin_4
  N29: Picoboard.pin_43, Picoprobe.pin_5
  N30: BNO055.3.3V, BNO055.INT_3V, BNO055.I2CADDR_3V

notes:
  stan
  © 2021 David Beaudette

custom parts:
  Raspberry Pi Pico: Raspberry Pi Pico. Based around the RP2040 microcontroller the Pico is a low cost microcontroller device bringing Raspberry Pi quality, cost, and easy of use to the microcontroller space. Jan 2021, Split part in to two versions: tht (this one) and SMD. This one will drill holes for a .1 in header in pcb to allow plugging in the module as well as providing pads to solder the module to the top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
  9-DOF Absolute Orientation IMU Fusion Breakout - BNO055: A MEMS accelerometer, magnetometer and gyroscope on a single die with a high speed ARM Cortex-M0 based processor to digest all the sensor data, abstract the sensor fusion and real time requirements away, and spit out data you can use in quaternions, Euler angles or vectors.
